# Fritzing sketch sketch (saved by Fritzing 1.0.4)
breadboards: 1

parts:
  LED1 = LED - 5mm [color="Red (633nm)" current=0.030A package="5 mm [THT]"]
  R1 = Resistor [tolerance=±5% power=0.25W resistance=220 package=THT]
  R2 = Resistor [tolerance=±5% power=0.25W resistance=220 package=THT]
  LED2 = LED - 5mm [color="Green (555nm)" current=0.030A package="5 mm [THT]"]
  Part1 = Adafruit Metro M4 AirLift Lite [part_number="Adafruit #4000"]
  Part2 = Soil Moisture Sensor

nets:
  N1: LED1.cathode, R1.Pin_1
  GND: LED1.anode, LED2.anode, Part1.GND, Part2.GND
  N2: R1.Pin_0, Part1.D2
  N3: R2.Pin_0, Part1.D1
  N4: R2.Pin_1, LED2.cathode
  N5: Part1.A0, Part2.VCC

custom parts:
  Adafruit Metro M4 AirLift Lite: This is the Adafruit Metro M4 AirLift and Metro AirLift Lite, a Metro M4 with an ESP32 WiFi co-processor built in!
